# Fritzing sketch shieldV1-Alex-Laptop-6 (saved by Fritzing 0.8.7b)
perfboards: 1

parts:
  J1 = Generic female header - 4 pins [form="♀ (female)" package=THT]
  3_3V = male pin header, 1 pin [form="♂ (male)"]
  Part1 = Arduino Mega 2560 (Rev3)
  J2 = female pin header, 3 pins [form="♀ (female)"]
  SW1 = DIP SWITCH [package=dipswitch-02]
  SW2 = DIP SWITCH [package=dipswitch-02]
  9DOF_Header = single row smd female pin header, 6 pins [form="♀ (female)"]
  Depth_Header = Generic female header - 4 pins [form="♀ (female)" package=THT]
  Part2 = 9-DOF Absolute Orientation IMU Fusion Breakout - BNO055

nets:
  N1: J1.pin1, 3_3V.pin1
  GND: J1.pin2, J2.pin3, 9DOF_Header.pin4, Depth_Header.pin3, Part2.GND
  N2: Part1.D21/SCL, Depth_Header.pin1
  N3: Part1.D20/SDA, Part1.SDA, 9DOF_Header.pin3, Depth_Header.pin2, Part2.SDA_5V
  N4: Part1.GND, SW1.4
  N5: Part1.D43, SW2.2
  N6: Part1.D45, SW2.1
  N7: Part1.D47, SW1.2
  N8: Part1.D49, SW1.1
  5V: J2.pin1, 9DOF_Header.pin6, Depth_Header.pin4, Part2.5.0V
  N9: SW1.3, SW2.3, SW2.4
  N10: 9DOF_Header.pin2, Part2.SCL_5V

notes:
  Red - 5V
  Orange - 3V
  Black - GND
  Blue - Analog

custom parts:
  Generic female header - 4 pins: Generic female header
  9-DOF Absolute Orientation IMU Fusion Breakout - BNO055: A MEMS accelerometer, magnetometer and gyroscope on a single die with a high speed ARM Cortex-M0 based processor to digest all the sensor data, abstract the sensor fusion and real time requirements away, and spit out data you can use in quaternions, Euler angles or vectors.
