# Fritzing sketch shieldV1-Alex-Laptop (saved by Fritzing 0.8.7b)
perfboards: 1

parts:
  J1 = Generic female header - 4 pins [form="♀ (female)" package=THT]
  3_3V = male pin header, 1 pin [form="♂ (male)"]
  Part1 = Arduino Mega 2560 (Rev3)
  J2 = female pin header, 3 pins [form="♀ (female)"]
  SW1 = DIP SWITCH [package=dipswitch-02]
  Part2 = 9-DOF Absolute Orientation IMU Fusion Breakout - BNO055
  SW2 = DIP SWITCH [package=dipswitch-02]
  J3 = single row smd female pin header, 6 pins [form="♀ (female)"]
  J4 = Generic female header - 4 pins [form="♀ (female)" package=THT]

nets:
  N1: J1.pin1, 3_3V.pin1
  N2: Part1.GND, SW1.3, SW1.4, SW2.3, SW2.4
  N3: Part1.D43, SW2.2
  N4: Part1.D45, SW2.1
  N5: Part1.D47, SW1.2
  N6: Part1.D49, SW1.1
  N7: J2.pin1, Part2.5.0V, J3.pin6, J4.pin4
  N8: J2.pin3, Part2.GND, J3.pin4, J4.pin3
  N9: Part2.3.3V, J3.pin5
  N10: Part2.SDA_5V, J3.pin3, J4.pin2
  N11: Part2.SCL_5V, J3.pin2, J4.pin1
  N12: Part2.RST_5V, J3.pin1

notes:
  Red - 5V
  Orange - 3V
  Black - GND
  Blue - Analog

custom parts:
  Generic female header - 4 pins: Generic female header
  9-DOF Absolute Orientation IMU Fusion Breakout - BNO055: A MEMS accelerometer, magnetometer and gyroscope on a single die with a high speed ARM Cortex-M0 based processor to digest all the sensor data, abstract the sensor fusion and real time requirements away, and spit out data you can use in quaternions, Euler angles or vectors.
