# Fritzing sketch shieldV2-Alex-Laptop-4 (saved by Fritzing 0.8.7b)
perfboards: 1

parts:
  J1 = Generic female header - 4 pins [form="♀ (female)" package=THT]
  Part1 = Arduino Mega 2560 (Rev3)
  J2 = female pin header, 3 pins [form="♀ (female)"]
  SW1 = DIP SWITCH [package=dipswitch-02]
  SW2 = DIP SWITCH [package=dipswitch-02]
  9DOF_Header = single row smd female pin header, 6 pins [form="♀ (female)"]
  Depth_Header = Generic female header - 4 pins [form="♀ (female)" package=THT]
  Part2 = 9-DOF Absolute Orientation IMU Fusion Breakout - BNO055
  9DOF_Plug = male pin header, 6 pins [form="♂ (male)"]
  3_3V = male pin header, 1 pin [form="♂ (male)"]

nets:
  N1: J1.pin1, 3_3V.pin1
  GND: J1.pin2, J2.pin3, 9DOF_Header.pin4, Depth_Header.pin3
  N2: J1.pin3, Part1.A6
  N3: J1.pin4, Part1.A7
  N4: Part1.D21/SCL, 9DOF_Header.pin2, Depth_Header.pin1
  N5: Part1.D20/SDA, Part1.SDA, 9DOF_Header.pin3, Depth_Header.pin2
  N6: Part1.GND, SW1.4
  N7: Part1.D43, SW2.2
  N8: Part1.D45, SW2.1
  N9: Part1.D47, SW1.2
  N10: Part1.D49, SW1.1
  5V: J2.pin1, 9DOF_Header.pin6, Depth_Header.pin4
  N11: SW1.3, SW2.3, SW2.4
  N12: Part2.5.0V, 9DOF_Plug.pin6
  N13: Part2.GND, 9DOF_Plug.pin4
  N14: Part2.SDA_5V, 9DOF_Plug.pin3
  N15: Part2.SCL_5V, 9DOF_Plug.pin2

notes:
  Red - 5V
  Orange - 3V
  Black - GND
  Blue - Analog

custom parts:
  Generic female header - 4 pins: Generic female header
  9-DOF Absolute Orientation IMU Fusion Breakout - BNO055: A MEMS accelerometer, magnetometer and gyroscope on a single die with a high speed ARM Cortex-M0 based processor to digest all the sensor data, abstract the sensor fusion and real time requirements away, and spit out data you can use in quaternions, Euler angles or vectors.
