# Fritzing sketch shieldV3-Alex-Laptop-2 (saved by Fritzing 0.8.7b)
perfboards: 2

parts:
  J1 = Generic female header - 4 pins [form="♀ (female)" package=THT]
  Part1 = Arduino Mega 2560 (Rev3)
  J2 = female pin header, 3 pins [form="♀ (female)"]
  SW2 = DIP SWITCH [package=dipswitch-02]
  9DOF_Header = single row smd female pin header, 6 pins [form="♀ (female)"]
  Depth_Header = Generic female header - 4 pins [form="♀ (female)" package=THT]
  Part2 = 9-DOF Absolute Orientation IMU Fusion Breakout - BNO055
  9DOF_Plug = male pin header, 6 pins [form="♂ (male)"]
  3_3V = male pin header, 1 pin [form="♂ (male)"]
  J3 = Generic female header - 4 pins [form="♀ (female)" package=THT]
  J4 = Generic female header - 4 pins [form="♀ (female)" package=THT]
  BEC_In = male pin header, 1 pin [form="♂ (male)"]
  Left_Thumbstick = Thumb Joystick
  Right_Thumbstick = Thumb Joystick
  LED1 = LED - 5mm [color="Green (570nm)" package="5 mm [THT]"]
  LED2 = LED - 5mm [color="Yellow (595nm)" package="5 mm [THT]"]
  J16 = Generic female header - 4 pins [form="♀ (female)" package=THT]
  J17 = male pin header, 4 pins [form="♂ (male)"]
  J18 = male pin header, 4 pins [form="♂ (male)"]
  J9 = male pin header, 4 pins [form="♂ (male)"]
  J10 = double row smd male pin header, 4 pins [form="♂ (male)"]
  J20 = male pin header, 3 pins [form="♂ (male)"]
  J21 = male pin header, 3 pins [form="♂ (male)"]
  J22 = male pin header, 3 pins [form="♂ (male)"]
  J23 = male pin header, 3 pins [form="♂ (male)"]
  J24 = male pin header, 3 pins [form="♂ (male)"]
  J25 = male pin header, 2 pins [form="♂ (male)"]
  J19 = male pin header, 3 pins [form="♂ (male)"]
  SW1 = DIP SWITCH [package=dipswitch-02]
  D1 = Rectifier Diode [part_number=1N4001 package="300 mil [THT]"]
  J26 = Basic Servo
  J30 = female pin header, 3 pins [form="♀ (female)"]
  J31 = female pin header, 3 pins [form="♀ (female)"]
  J32 = Basic Servo
  J34 = Basic Servo
  J35 = female pin header, 3 pins [form="♀ (female)"]
  J36 = Basic Servo
  J33 = female pin header, 3 pins [form="♀ (female)"]
  ESC_Fan = DC Motor
  J37 = female pin header, 2 pins [form="♀ (female)"]
  J38 = Basic Servo [part_number=ESC]
  J39 = female pin header, 3 pins [form="♀ (female)"]
  J40 = female pin header, 3 pins [form="♀ (female)"]
  C2 = Electrolytic Capacitor [package="100 mil [THT, electrolytic]"]
  C3 = Electrolytic Capacitor [package="300 mil [THT, electrolytic]"]

nets:
  N1: J1.pin1, Part1.3V3, 3_3V.pin1
  GND: J1.pin2, Part1.GND, J2.pin3, 9DOF_Header.pin4, Depth_Header.pin3, J3.pin4, SW1.4, C2.-
  N2: J1.pin3, Part1.A6
  N3: J1.pin4, Part1.A7
  N4: Part1.A8, J16.pin1
  N5: Part1.A9, J16.pin2
  N6: Part1.A10, J16.pin3
  N7: Part1.A11, J16.pin4
  N8: Part1.D21/SCL, 9DOF_Header.pin2, Depth_Header.pin1
  N9: Part1.D20/SDA, Part1.SDA, 9DOF_Header.pin3, Depth_Header.pin2
  N10: Part1.VIN, D1.cathode
  N11: Part1.D25, J4.pin1
  N12: Part1.D27, J4.pin2
  N13: Part1.D29, J4.pin3
  N14: Part1.D31, J4.pin4
  N15: Part1.D33, J3.pin1
  N16: Part1.D35, J3.pin2
  N17: Part1.D43, SW2.2
  N18: Part1.D45, SW2.1
  N19: Part1.D47, SW1.2
  N20: Part1.D49, SW1.1
  5V: J2.pin1, 9DOF_Header.pin6, Depth_Header.pin4
  N21: SW2.3, SW2.4, SW1.3
  N22: Part2.5.0V, 9DOF_Plug.pin6
  N23: Part2.GND, 9DOF_Plug.pin4
  N24: Part2.SDA_5V, 9DOF_Plug.pin3
  N25: Part2.SCL_5V, 9DOF_Plug.pin2
  VIN: J3.pin3, BEC_In.pin1, D1.anode, C2.+
  GND_2: Left_Thumbstick.GND, Right_Thumbstick.GND, LED1.cathode, LED2.cathode, J17.pin2
  N26: Left_Thumbstick.HORZ, J18.pin4
  N27: Left_Thumbstick.VERT, J18.pin1
  VCC: Left_Thumbstick.VCC, Right_Thumbstick.VCC, J17.pin1
  N28: Right_Thumbstick.SEL, J18.pin3
  N29: Right_Thumbstick.VERT, J18.pin2
  N30: LED1.anode, J17.pin4
  N31: LED2.anode, J17.pin3
  N32: J9.pin1, J10.pin4, J20.pin1, J21.pin1, J22.pin1, J23.pin1, J24.pin1, J25.pin1, J19.pin1, C3.-
  N33: J9.pin2, J19.pin3
  N34: J9.pin3, J20.pin3
  N35: J9.pin4, J21.pin3
  N36: J10.pin1, J22.pin3
  N37: J10.pin2, J23.pin3
  N38: J10.pin3, J20.pin2, J21.pin2, J22.pin2, J23.pin2, J24.pin2, J25.pin2, J19.pin2, C3.+
  N39: J26.gnd, J30.pin1
  N40: J26.vcc, J30.pin2
  N41: J26.pulse, J30.pin3
  N42: J31.pin1, J32.gnd
  N43: J31.pin2, J32.vcc
  N44: J31.pin3, J32.pulse
  N45: J34.gnd, J33.pin1
  N46: J34.vcc, J33.pin2
  N47: J34.pulse, J33.pin3
  N48: J35.pin1, J36.gnd
  N49: J35.pin2, J36.vcc
  N50: J35.pin3, J36.pulse
  N51: ESC_Fan.pin_1, J37.pin2
  N52: ESC_Fan.pin_2, J37.pin1
  N53: J38.gnd, J39.pin1, J40.pin1
  N54: J38.vcc, J39.pin2, J40.pin2
  N55: J38.pulse, J39.pin3

notes:
  Red - 5V
  Orange - 3V
  Black - GND
  Blue - Analog
  Pink - Input Power
  Green - I2C
  Yellow - PWM
  ESC, Battery, and BEC
  Servo representing ESC and motor

custom parts:
  Generic female header - 4 pins: Generic female header
  9-DOF Absolute Orientation IMU Fusion Breakout - BNO055: A MEMS accelerometer, magnetometer and gyroscope on a single die with a high speed ARM Cortex-M0 based processor to digest all the sensor data, abstract the sensor fusion and real time requirements away, and spit out data you can use in quaternions, Euler angles or vectors.
  Electrolytic Capacitor: A small electrolytic capacitor
  Electrolytic Capacitor: 1000µF electrolytic capacitor
